# Fritzing sketch goodhands (saved by Fritzing 0.8.7b)
breadboards: 1

parts:
  Uno = Arduino Uno (Rev3)
  Middle = Electrolytic Capacitor [capacitance=1µF package="100 mil [THT, electrolytic]"]  # not connected
  Ring = Electrolytic Capacitor [capacitance=1µF package="100 mil [THT, electrolytic]"]
  Pinky = Electrolytic Capacitor [capacitance=1µF package="100 mil [THT, electrolytic]"]  # not connected
  Pointer = Electrolytic Capacitor [capacitance=1µF package="100 mil [THT, electrolytic]"]  # not connected
  Pinky_2 = LED - 5mm [color="Red (633nm)" package="5 mm [THT]"]
  Ring_2 = LED - 5mm [color="Red (633nm)" package="5 mm [THT]"]
  MIddle = LED - 5mm [color="Red (633nm)" package="5 mm [THT]"]
  Pointer_2 = LED - 5mm [color="Red (633nm)" package="5 mm [THT]"]
  R5 = Resistor [tolerance=±5% resistance=220 package=THT]
  R6 = Resistor [tolerance=±5% resistance=220 package=THT]
  R7 = Resistor [tolerance=±5% resistance=220 package=THT]
  R8 = Resistor [tolerance=±5% resistance=220 package=THT]
  1_M = 1 MΩ Resistor [package=THT]
  1_M_2 = 1 MΩ Resistor [package=THT]
  1_M_3 = 1 MΩ Resistor [package=THT]
  1_M_4 = 1 MΩ Resistor [package=THT]

nets:
  N1: Uno.D8, 1_M_4.Pin_1
  N2: Uno.D9_PWM, Pointer_2.anode
  N3: Uno.D10_PWM/SS, 1_M_2.Pin_1
  N4: Uno.GND, R5.Pin_1, R6.Pin_1, R7.Pin_1, R8.Pin_1
  N5: Uno.D2, 1_M.Pin_0, 1_M_2.Pin_0, 1_M_3.Pin_0, 1_M_4.Pin_0
  N6: Uno.D3_PWM, Pinky_2.anode
  N7: Uno.D4, 1_M.Pin_1
  N8: Uno.D5_PWM, Ring_2.anode
  N9: Uno.D6_PWM, Ring.-, 1_M_3.Pin_1
  N10: Uno.D7, MIddle.anode
  N11: Pinky_2.cathode, R5.Pin_0
  N12: Ring_2.cathode, R6.Pin_0
  N13: MIddle.cathode, R7.Pin_0
  N14: Pointer_2.cathode, R8.Pin_0

notes:
  SEND pin 2
  RECEIVE PINS 4, 6, 8, 10
  Pointer Finger
  Middle Finger
  Ring Finger
  Pinky Finger
  SIGNAL lights

custom parts:
  1 MΩ Resistor: A generic resistor (0.25W)
